// Logisim project Design_and_Simulation_of_a_4_Bit_Binary_Arithemetic_Using_Logisim Circuit (1).circ as structural Verilog: 1 circuit, main circuit main
module main (
  input  [3:0] in_1,
  input  [1:0] in_2,
  input  [3:0] in_3,
  output [3:0] out_4
);

  wire [3:0] adder_1_out, and_1_out, or_1_out, subtractor_1_out;

  assign or_1_out = in_3 | in_1;  // OR_Gate or_1, 4 bits wide
  assign and_1_out = in_3 & in_1;  // AND_Gate and_1, 4 bits wide
  Adder #(.width(4)) adder_1 (.a(in_3), .b(in_1), .out(adder_1_out));  // open: cin, cout
  Subtractor #(.width(4)) subtractor_1 (.a(in_3), .b(in_1), .out(subtractor_1_out));  // open: bin, bout
  Multiplexer #(.select(2), .width(4)) multiplexer_1 (
    .in0(or_1_out), .in1(and_1_out), .in2(adder_1_out), .in3(subtractor_1_out), .out(out_4), .sel(in_2));  // open: en
endmodule
